// Digital circuit PhaseClockGen.dig as structural Verilog
module PhaseClockGen (
  input  clk
);

  wire _74174_1_pin2, _74174_1_pin5, _74174_1_pin7, _74174_1_pin10, _74174_1_pin12, _74174_1_pin15,
       button_1_out, nor_1_out;

  Button #(.activeLow("true")) button_1 (.out(button_1_out));
  nor nor_1 (nor_1_out, _74174_1_pin10, _74174_1_pin15, _74174_1_pin12);
  _74174 _74174_1 (
    .pin1(button_1_out), .pin2(_74174_1_pin2), .pin3(nor_1_out), .pin4(_74174_1_pin2), .pin5(_74174_1_pin5),
    .pin6(_74174_1_pin5), .pin7(_74174_1_pin7), .pin8(1'b0), .pin9(clk), .pin10(_74174_1_pin10),
    .pin11(_74174_1_pin7), .pin12(_74174_1_pin12), .pin13(_74174_1_pin10), .pin14(_74174_1_pin12),
    .pin15(_74174_1_pin15), .pin16(1'b1));
  // Probe CLK_1 on _74174_1_pin2
  // Probe CLK_2 on _74174_1_pin5
  // Probe CLK_3 on _74174_1_pin7
  // Probe CLK_4 on _74174_1_pin10
  // Probe CLK_5 on _74174_1_pin12
  // Probe CLK_6 on _74174_1_pin15
  LED led_1 (.in(_74174_1_pin2));
  LED led_2 (.in(_74174_1_pin5));
  LED led_3 (.in(_74174_1_pin7));
  LED led_4 (.in(_74174_1_pin10));
  LED led_5 (.in(_74174_1_pin12));
  LED led_6 (.in(_74174_1_pin15));

  // Notes on the sheet:
  //   NAND - Q1,Q2,Q3 - 4phase, 3:1 duty
  //   NOR - Q1,Q2,Q3 - 4phase, 1:3 duty
  //   NOR - Q2,Q3,Q4 - 6phase, 2:6 duty
  //   NOR - Q3,Q4,Q5 - 5phase, 3:5 duty
  //   NOR - Q1,Q2 - 3phase, 1:2 duty
  //   NOT - Q1 - 2phase, 1:1 duty
  //   NOT - Q2 - 2phase, 2:2 duty
endmodule
